# Fritzing sketch LedParpadeandoSketch (saved by Fritzing 0.9.3b)
circuit board: 8.46667cm x 5.64444cm
breadboards: 1

parts:
  Componente1 = Arduino Uno (Rev3)
  LED1 = LED - 5mm [color="Red (633nm)" package="5 mm [THT]"]
  R1 = Resistor [tolerance=±5% resistance=330 package=THT]

nets:
  N1: Componente1.D13/SCK, LED1.anode
  N2: Componente1.GND, R1.Pin_0
  N3: LED1.cathode, R1.Pin_1
