# Fritzing sketch LedIntermitentePotenciometro (saved by Fritzing 0.9.3b)
breadboards: 1

parts:
  Componente1 = Arduino Uno (Rev3)
  LED1 = LED - 5mm [color="Red (633nm)" package="5 mm [THT]"]
  R1 = Trimmer Potentiometer [maximum_resistance=10kΩ package=THT]
  R2 = Resistor [tolerance=±5% resistance=330 package="2512 [SMD]"]

nets:
  N1: Componente1.D13/SCK, R1.leg2
  N2: Componente1.GND, R2.Pin_0
  N3: LED1.cathode, R1.leg1, R2.Pin_1
  N4: LED1.anode, R1.wiper
